// Logisim project 2.circ as structural Verilog: 12 circuits, main circuit main
module main (
);

  wire _1colod, _2colod, _3colod, _4colod, _5colod, _6colod, _7colod, Clock, controlled_buffer_4_out,
       cur_move, d_ff_1_q, data_ins, data_o, fst_usage, gen_done, generator_1_gen_done, generator_1_l_d,
       IAck, ins_p, IO_o, memory, move1, move2, move3, move4, move5, move6, move7, move_done,
       multiplexer_1_out, multiplexer_2_out, multiplexer_3_out, multiplexer_4_out, multiplexer_5_out,
       multiplexer_6_out, multiplexer_7_out, multiplexer_16_out, not_1_out, not_3_out, or_2_p6,
       pull_resistor_1_node, read_write, rep1, rep2, rep3, rep4, rep5, rep6, rep7, reset, sent_done,
       undriven, vector_p, write_sentinels_1_clock_gen, write_sentinels_1_l_d;
  wire [0:0] and_1_out;
  wire [7:0] addr, buffer_1_out, buffer_2_out, buffer_3_out, cdm_8_mark5_1_p8, cdm_8_mark5_1_p9, com1, com2,
       com3, com4, com5, com6, com7, controlled_buffer_6_out, counter_1_q, cur_command, data_base,
       generator_1_address, generator_1_data, multiplexer_10_out, multiplexer_15_out,
       n1_colod_1_updated_program, n2_colod_1_updated_program, n3_colod_1_p2, n4_colod_1_p3, n5_colod_1_p3,
       n6_colod_1_p3, n7_colod_1_p3, new_com, or_1_p5, write_sentinels_1_address, write_sentinels_1_data;

  Hex_Digit_Display hex_digit_display_1 (.value(cur_command[7:4]));  // open: dp
  D_Flip_Flop d_ff_1 (.Q(d_ff_1_q), .preset(undriven), .reset(IAck));  // open: clk, D, Qn, en
  and and_1 (and_1_out[0], addr[4], addr[5], addr[6], addr[7]);
  Hex_Digit_Display hex_digit_display_2 (.value(cur_command[3:0]));  // open: dp
  Multiplexer #(.enable("false")) multiplexer_1 (.in0(_1colod), .in1(1'b0), .out(multiplexer_1_out), .sel(rep1));
  Multiplexer #(.enable("false")) multiplexer_2 (.in0(_2colod), .in1(1'b0), .out(multiplexer_2_out), .sel(rep2));
  Multiplexer #(.enable("false")) multiplexer_3 (.in0(_3colod), .in1(1'b0), .out(multiplexer_3_out), .sel(rep3));
  Multiplexer #(.enable("false")) multiplexer_4 (.in0(_4colod), .in1(1'b0), .out(multiplexer_4_out), .sel(rep4));
  Multiplexer #(.enable("false")) multiplexer_5 (.in0(_5colod), .in1(1'b0), .out(multiplexer_5_out), .sel(rep5));
  Multiplexer #(.enable("false")) multiplexer_6 (.in0(_6colod), .in1(1'b0), .out(multiplexer_6_out), .sel(rep6));
  Multiplexer #(.enable("false")) multiplexer_7 (.in0(_7colod), .in1(1'b0), .out(multiplexer_7_out), .sel(rep7));
  Clock clock_1 (.out(Clock));
  Decoder #(.select(2), .disabled(0)) decoder_1 (
    .out0(ins_p), .out1(vector_p), .out2(data_o), .out3(IO_o), .sel({data_ins, and_1_out[0]}), .en(memory));
  // CdM_8_mark5 cdm_8_mark5_1: pin names not known; wires that end beside it: d_ff_1_q, 3'b000, IAck, data_ins, memory, read_write, addr, cdm_8_mark5_1_p8, cdm_8_mark5_1_p9
  assign cdm_8_mark5_1_p9 = read_write ? data_base : 8'bz;  // Controlled_Buffer controlled_buffer_1
  _1_colod u_1_colod_1 (
    ._1(multiplexer_1_out), .cur_command(cur_command), .move_done_updated(move1),
    .updated_program(n1_colod_1_updated_program), .repeated_command(rep1));
  _2_colod u_2_colod_1 (
    ._2(multiplexer_2_out), .updated_program(n2_colod_1_updated_program), .cur_command(cur_command),
    .move_done_updated(move2), .repeated_command(rep2));
  // _3_colod 3_colod_1: pin names not known; wires that end beside it: cur_command, n3_colod_1_p2, move3, rep3
  // _4_colod 4_colod_1: pin names not known; wires that end beside it: multiplexer_4_out, cur_command, n4_colod_1_p3, move4, rep4
  // _5_colod 5_colod_1: pin names not known; wires that end beside it: multiplexer_5_out, cur_command, n5_colod_1_p3, move5, rep5
  // _6_colod 6_colod_1: pin names not known; wires that end beside it: multiplexer_6_out, cur_command, n6_colod_1_p3, move6, rep6
  // _7_colod 7_colod_1: pin names not known; wires that end beside it: multiplexer_7_out, cur_command, n7_colod_1_p3, move7, rep7
  assign data_base = not_1_out ? cdm_8_mark5_1_p8 : 8'bz;  // Controlled_Buffer controlled_buffer_2
  not not_1 (not_1_out, read_write);
  Multiplexer #(.width(8), .enable("false")) multiplexer_8 (
    .in0(n1_colod_1_updated_program), .in1(cur_command), .out(com1), .sel(rep1));
  Multiplexer #(.width(8), .enable("false")) multiplexer_9 (
    .in0(n2_colod_1_updated_program), .out(com2), .sel(rep2));  // open: in1
  Multiplexer #(.width(8), .enable("false")) multiplexer_10 (
    .in0(n3_colod_1_p2), .out(multiplexer_10_out), .sel(rep3));  // open: in1
  Multiplexer #(.width(8), .enable("false")) multiplexer_11 (.in0(n4_colod_1_p3), .out(com4), .sel(rep4));  // open: in1
  Multiplexer #(.width(8), .enable("false")) multiplexer_12 (.in0(n5_colod_1_p3), .out(com5), .sel(rep5));  // open: in1
  Multiplexer #(.width(8), .enable("false")) multiplexer_13 (.in0(n6_colod_1_p3), .out(com6), .sel(rep6));  // open: in1
  Multiplexer #(.width(8), .enable("false")) multiplexer_14 (.in0(n7_colod_1_p3), .out(com7), .sel(rep7));  // open: in1
  assign buffer_1_out = generator_1_address;  // Buffer buffer_1, 8 bits wide
  assign buffer_1_out = gen_done ? write_sentinels_1_address : 8'bz;  // Controlled_Buffer controlled_buffer_3
  Multiplexer #(.width(8), .enable("false")) multiplexer_15 (
    .in0({8{1'b0}}), .in1(new_com), .out(multiplexer_15_out), .sel(fst_usage));
  Multiplexer #(.enable("false")) multiplexer_16 (
    .in0(1'b0), .in1(move_done), .out(multiplexer_16_out), .sel(fst_usage));
  not not_2 (gen_done, generator_1_gen_done);
  assign controlled_buffer_4_out = gen_done ? write_sentinels_1_clock_gen : 1'bz;  // Controlled_Buffer controlled_buffer_4
  Pull_Resistor pull_resistor_1 (.node(pull_resistor_1_node));
  assign pull_resistor_1_node = gen_done ? Clock : 1'bz;  // Controlled_Buffer controlled_buffer_5
  // OR_Gate #(.width(8)) or_1: pin names not known; wires that end beside it: com3, com5, com7, com1, or_1_p5
  // OR_Gate or_2: pin names not known; wires that end beside it: com7, move3, move5, move7, move1, or_2_p6
  assign controlled_buffer_6_out = sent_done ? multiplexer_15_out : 8'bz;  // Controlled_Buffer controlled_buffer_6
  assign cur_move = sent_done ? multiplexer_16_out : 1'bz;  // Controlled_Buffer controlled_buffer_7
  Counter counter_1 (.Q(counter_1_q), .clk(sent_done), .clr(reset));  // open: load, D, count, carry
  assign buffer_2_out = buffer_3_out;  // Buffer buffer_2, 8 bits wide
  RAM ram_1 (
    .addr(buffer_1_out), .data(buffer_2_out), .clk(controlled_buffer_4_out), .ld(generator_1_l_d), .clr(reset));  // open: sel
  generator generator_1 (
    .clock(Clock), .reset(reset), .data(generator_1_data), .address(generator_1_address),
    .clock_gen(controlled_buffer_4_out), .l_d(generator_1_l_d), .gen_done(generator_1_gen_done));
  assign generator_1_l_d = gen_done ? write_sentinels_1_l_d : 1'bz;  // Controlled_Buffer controlled_buffer_8
  write_sentinels write_sentinels_1 (
    .data(write_sentinels_1_data), .clock(pull_resistor_1_node), .reset(reset),
    .address(write_sentinels_1_address), .clock_gen(write_sentinels_1_clock_gen),
    .l_d(write_sentinels_1_l_d), .sent_writing_done(sent_done));
  assign new_com = fst_usage ? or_1_p5 : 8'bz;  // Controlled_Buffer controlled_buffer_9
  Pull_Resistor pull_resistor_2 (.node(new_com));
  Pull_Resistor pull_resistor_3 (.node(move_done));
  assign move_done = fst_usage ? or_2_p6 : 1'bz;  // Controlled_Buffer controlled_buffer_10
  Pull_Resistor pull_resistor_4 (.node(controlled_buffer_6_out));
  Pull_Resistor pull_resistor_5 (.node(cur_command));
  assign cur_command = fst_usage ? controlled_buffer_6_out : 8'bz;  // Controlled_Buffer controlled_buffer_11
  Pull_Resistor pull_resistor_6 (.node(cur_move));
  Comparator comparator_1 (.a(counter_1_q), .b({8{1'b0}}), .gt(fst_usage));  // open: eq, lt
  Button button_1 (.out(reset));
  not not_3 (not_3_out, not_3_out);
  assign buffer_3_out = generator_1_data;  // Buffer buffer_3, 8 bits wide
  assign buffer_3_out = gen_done ? write_sentinels_1_data : 8'bz;  // Controlled_Buffer controlled_buffer_12
  Button button_2 (.out(_1colod));
  Hex_Digit_Display hex_digit_display_3 ();  // open: value, dp
  Hex_Digit_Display hex_digit_display_4 ();  // open: value, dp
  Hex_Digit_Display hex_digit_display_5 ();  // open: value, dp
  Hex_Digit_Display hex_digit_display_6 ();  // open: value, dp
  Hex_Digit_Display hex_digit_display_7 ();  // open: value, dp
  Hex_Digit_Display hex_digit_display_8 ();  // open: value, dp
  Hex_Digit_Display hex_digit_display_9 ();  // open: value, dp
  Hex_Digit_Display hex_digit_display_10 ();  // open: value, dp
  Button button_3 (.out(_2colod));
  Hex_Digit_Display hex_digit_display_11 ();  // open: value, dp
  Hex_Digit_Display hex_digit_display_12 ();  // open: value, dp
  Hex_Digit_Display hex_digit_display_13 ();  // open: value, dp
  Hex_Digit_Display hex_digit_display_14 ();  // open: value, dp
  Hex_Digit_Display hex_digit_display_15 ();  // open: value, dp
  Hex_Digit_Display hex_digit_display_16 ();  // open: value, dp
  Hex_Digit_Display hex_digit_display_17 ();  // open: value, dp
  Hex_Digit_Display hex_digit_display_18 ();  // open: value, dp
  Hex_Digit_Display hex_digit_display_19 ();  // open: value, dp
  Button button_4 (.out(_3colod));
  Hex_Digit_Display hex_digit_display_20 ();  // open: value, dp
  Hex_Digit_Display hex_digit_display_21 ();  // open: value, dp
  Hex_Digit_Display hex_digit_display_22 ();  // open: value, dp
  Hex_Digit_Display hex_digit_display_23 ();  // open: value, dp
  Hex_Digit_Display hex_digit_display_24 ();  // open: value, dp
  Hex_Digit_Display hex_digit_display_25 ();  // open: value, dp
  Hex_Digit_Display hex_digit_display_26 ();  // open: value, dp
  Hex_Digit_Display hex_digit_display_27 ();  // open: value, dp
  Hex_Digit_Display hex_digit_display_28 ();  // open: value, dp
  Hex_Digit_Display hex_digit_display_29 ();  // open: value, dp
  Button button_5 (.out(_4colod));
  Hex_Digit_Display hex_digit_display_30 ();  // open: value, dp
  Hex_Digit_Display hex_digit_display_31 ();  // open: value, dp
  Hex_Digit_Display hex_digit_display_32 ();  // open: value, dp
  Hex_Digit_Display hex_digit_display_33 ();  // open: value, dp
  Hex_Digit_Display hex_digit_display_34 ();  // open: value, dp
  Hex_Digit_Display hex_digit_display_35 ();  // open: value, dp
  Hex_Digit_Display hex_digit_display_36 ();  // open: value, dp
  Hex_Digit_Display hex_digit_display_37 ();  // open: value, dp
  Hex_Digit_Display hex_digit_display_38 ();  // open: value, dp
  Hex_Digit_Display hex_digit_display_39 ();  // open: value, dp
  Hex_Digit_Display hex_digit_display_40 ();  // open: value, dp
  Button button_6 (.out(_5colod));
  Hex_Digit_Display hex_digit_display_41 ();  // open: value, dp
  Hex_Digit_Display hex_digit_display_42 ();  // open: value, dp
  Hex_Digit_Display hex_digit_display_43 ();  // open: value, dp
  Hex_Digit_Display hex_digit_display_44 ();  // open: value, dp
  Hex_Digit_Display hex_digit_display_45 ();  // open: value, dp
  Hex_Digit_Display hex_digit_display_46 ();  // open: value, dp
  Hex_Digit_Display hex_digit_display_47 ();  // open: value, dp
  Hex_Digit_Display hex_digit_display_48 ();  // open: value, dp
  Hex_Digit_Display hex_digit_display_49 ();  // open: value, dp
  Hex_Digit_Display hex_digit_display_50 ();  // open: value, dp
  Hex_Digit_Display hex_digit_display_51 ();  // open: value, dp
  Hex_Digit_Display hex_digit_display_52 ();  // open: value, dp
  Button button_7 (.out(_6colod));
  Hex_Digit_Display hex_digit_display_53 ();  // open: value, dp
  Hex_Digit_Display hex_digit_display_54 ();  // open: value, dp
  Hex_Digit_Display hex_digit_display_55 ();  // open: value, dp
  Hex_Digit_Display hex_digit_display_56 ();  // open: value, dp
  Hex_Digit_Display hex_digit_display_57 ();  // open: value, dp
  Hex_Digit_Display hex_digit_display_58 ();  // open: value, dp
  Hex_Digit_Display hex_digit_display_59 ();  // open: value, dp
  Hex_Digit_Display hex_digit_display_60 ();  // open: value, dp
  Hex_Digit_Display hex_digit_display_61 ();  // open: value, dp
  Hex_Digit_Display hex_digit_display_62 ();  // open: value, dp
  Hex_Digit_Display hex_digit_display_63 ();  // open: value, dp
  Hex_Digit_Display hex_digit_display_64 ();  // open: value, dp
  Hex_Digit_Display hex_digit_display_65 ();  // open: value, dp
  Button button_8 (.out(_7colod));
  Hex_Digit_Display hex_digit_display_66 ();  // open: value, dp
  Hex_Digit_Display hex_digit_display_67 ();  // open: value, dp
  Hex_Digit_Display hex_digit_display_68 ();  // open: value, dp
  Hex_Digit_Display hex_digit_display_69 ();  // open: value, dp
  Hex_Digit_Display hex_digit_display_70 ();  // open: value, dp
  Hex_Digit_Display hex_digit_display_71 ();  // open: value, dp
  Hex_Digit_Display hex_digit_display_72 ();  // open: value, dp
  Hex_Digit_Display hex_digit_display_73 ();  // open: value, dp
  Hex_Digit_Display hex_digit_display_74 ();  // open: value, dp
  Hex_Digit_Display hex_digit_display_75 ();  // open: value, dp
  Hex_Digit_Display hex_digit_display_76 ();  // open: value, dp
  Hex_Digit_Display hex_digit_display_77 ();  // open: value, dp
  Hex_Digit_Display hex_digit_display_78 ();  // open: value, dp
  Hex_Digit_Display hex_digit_display_79 ();  // open: value, dp

  // Notes on the sheet:
  //   from
  //   to
endmodule

module _1_colod (
  input  _1,
  input  [7:0] cur_command,
  output [7:0] updated_program,
  output repeated_command,
  output move_done_updated
);

  wire _1st_done, _2st_done, and_1_out, and_2_out, and_3_out, and_4_out, and_5_out, and_6_out, and_7_out,
       and_8_out, or_3_out, or_4_out;

  Comparator #(.width(4), .mode("unsigned")) comparator_1 (
    .a(4'b0001), .b(cur_command[3:0]), .eq(repeated_command));  // open: gt, lt
  or or_1 (_1st_done, cur_command[0], cur_command[1], cur_command[2], cur_command[3]);
  or or_2 (_2st_done, cur_command[4], cur_command[5], cur_command[6], cur_command[7]);
  and and_1 (and_1_out, _1st_done, _2st_done);
  or or_3 (or_3_out, updated_program[0], updated_program[1], updated_program[2], updated_program[3]);
  and and_2 (and_2_out, or_3_out, or_4_out);
  or or_4 (or_4_out, updated_program[4], updated_program[5], updated_program[6], updated_program[7]);
  or or_5 (move_done_updated, and_1_out, and_2_out);
  and and_3 (and_3_out, _1st_done, _1, _2st_done, ~repeated_command);  // AND_Gate
  and and_4 (and_4_out, _1st_done, ~_1, _2st_done, ~repeated_command);  // AND_Gate
  and and_5 (and_5_out, _1st_done, _1, ~_2st_done, ~repeated_command);  // AND_Gate
  and and_6 (and_6_out, ~_1st_done, _1, ~_2st_done, ~repeated_command);  // AND_Gate
  and and_7 (and_7_out, _1st_done, ~_1, ~_2st_done, ~repeated_command);  // AND_Gate
  and and_8 (and_8_out, ~_1st_done, ~_1, ~_2st_done, ~repeated_command);  // AND_Gate
  assign updated_program = and_3_out ? cur_command : 8'bz;  // Controlled_Buffer controlled_buffer_1
  assign updated_program = and_4_out ? cur_command : 8'bz;  // Controlled_Buffer controlled_buffer_2
  assign updated_program = and_5_out ? {4'b0001, cur_command[3:0]} : 8'bz;  // Controlled_Buffer controlled_buffer_3
  assign updated_program = and_6_out ? {cur_command[7:4], 4'b0001} : 8'bz;  // Controlled_Buffer controlled_buffer_4
  assign updated_program = and_7_out ? cur_command : 8'bz;  // Controlled_Buffer controlled_buffer_5
  assign updated_program = and_8_out ? cur_command : 8'bz;  // Controlled_Buffer controlled_buffer_6
  assign updated_program = repeated_command ? cur_command : 8'bz;  // Controlled_Buffer controlled_buffer_7

  // Other names for the same wires on the sheet: case2[3:0] = cur_command[3:0]; case3[7:0] = cur_command;
  //   command[7:0] = cur_command; case1[7:4] = cur_command[7:4]; not_equal = repeated_command;
  //   res[7:0] = updated_program
endmodule

module _2_colod (
  input  _2,
  input  [7:0] cur_command,
  output [7:0] updated_program,
  output repeated_command,
  output move_done_updated
);

  wire _1st_done, _2st_done, and_1_out, and_2_out, and_3_out, and_4_out, and_5_out, and_6_out, and_7_out,
       and_8_out, or_3_out, or_4_out;

  Comparator #(.width(4), .mode("unsigned")) comparator_1 (
    .a(4'b0010), .b(cur_command[3:0]), .eq(repeated_command));  // open: gt, lt
  or or_1 (_1st_done, cur_command[0], cur_command[1], cur_command[2], cur_command[3]);
  or or_2 (_2st_done, cur_command[4], cur_command[5], cur_command[6], cur_command[7]);
  and and_1 (and_1_out, _1st_done, _2st_done);
  or or_3 (or_3_out, updated_program[0], updated_program[1], updated_program[2], updated_program[3]);
  and and_2 (and_2_out, or_3_out, or_4_out);
  or or_4 (or_4_out, updated_program[4], updated_program[5], updated_program[6], updated_program[7]);
  or or_5 (move_done_updated, and_1_out, and_2_out);
  and and_3 (and_3_out, _1st_done, _2, _2st_done, ~repeated_command);  // AND_Gate
  and and_4 (and_4_out, _1st_done, ~_2, _2st_done, ~repeated_command);  // AND_Gate
  and and_5 (and_5_out, _1st_done, _2, ~_2st_done, ~repeated_command);  // AND_Gate
  and and_6 (and_6_out, ~_1st_done, _2, ~_2st_done, ~repeated_command);  // AND_Gate
  and and_7 (and_7_out, _1st_done, ~_2, ~_2st_done, ~repeated_command);  // AND_Gate
  and and_8 (and_8_out, ~_1st_done, ~_2, ~_2st_done, ~repeated_command);  // AND_Gate
  assign updated_program = and_3_out ? cur_command : 8'bz;  // Controlled_Buffer controlled_buffer_1
  assign updated_program = and_4_out ? cur_command : 8'bz;  // Controlled_Buffer controlled_buffer_2
  assign updated_program = and_5_out ? {4'b0010, cur_command[3:0]} : 8'bz;  // Controlled_Buffer controlled_buffer_3
  assign updated_program = and_6_out ? {cur_command[7:4], 4'b0010} : 8'bz;  // Controlled_Buffer controlled_buffer_4
  assign updated_program = and_7_out ? cur_command : 8'bz;  // Controlled_Buffer controlled_buffer_5
  assign updated_program = and_8_out ? cur_command : 8'bz;  // Controlled_Buffer controlled_buffer_6
  assign updated_program = repeated_command ? cur_command : 8'bz;  // Controlled_Buffer controlled_buffer_7

  // Other names for the same wires on the sheet: case2[3:0] = cur_command[3:0]; case3[7:0] = cur_command;
  //   command[7:0] = cur_command; case1[7:4] = cur_command[7:4]; not_equal = repeated_command;
  //   res[7:0] = updated_program
endmodule

module _3_colod (
  input  _3,
  input  [7:0] cur_command,
  output [7:0] updated_program,
  output repeated_command,
  output move_done_updated
);

  wire _1st_done, _2st_done, and_1_out, and_2_out, and_3_out, and_4_out, and_5_out, and_6_out, and_7_out,
       and_8_out, or_3_out, or_4_out;

  Comparator #(.width(4), .mode("unsigned")) comparator_1 (
    .a(4'b0011), .b(cur_command[3:0]), .eq(repeated_command));  // open: gt, lt
  or or_1 (_1st_done, cur_command[0], cur_command[1], cur_command[2], cur_command[3]);
  or or_2 (_2st_done, cur_command[4], cur_command[5], cur_command[6], cur_command[7]);
  and and_1 (and_1_out, _1st_done, _2st_done);
  or or_3 (or_3_out, updated_program[0], updated_program[1], updated_program[2], updated_program[3]);
  and and_2 (and_2_out, or_3_out, or_4_out);
  or or_4 (or_4_out, updated_program[4], updated_program[5], updated_program[6], updated_program[7]);
  or or_5 (move_done_updated, and_1_out, and_2_out);
  and and_3 (and_3_out, _1st_done, _3, _2st_done, ~repeated_command);  // AND_Gate
  and and_4 (and_4_out, _1st_done, ~_3, _2st_done, ~repeated_command);  // AND_Gate
  and and_5 (and_5_out, _1st_done, _3, ~_2st_done, ~repeated_command);  // AND_Gate
  and and_6 (and_6_out, ~_1st_done, _3, ~_2st_done, ~repeated_command);  // AND_Gate
  and and_7 (and_7_out, _1st_done, ~_3, ~_2st_done, ~repeated_command);  // AND_Gate
  and and_8 (and_8_out, ~_1st_done, ~_3, ~_2st_done, ~repeated_command);  // AND_Gate
  assign updated_program = and_3_out ? cur_command : 8'bz;  // Controlled_Buffer controlled_buffer_1
  assign updated_program = and_4_out ? cur_command : 8'bz;  // Controlled_Buffer controlled_buffer_2
  assign updated_program = and_5_out ? {4'b0011, cur_command[3:0]} : 8'bz;  // Controlled_Buffer controlled_buffer_3
  assign updated_program = and_6_out ? {cur_command[7:4], 4'b0011} : 8'bz;  // Controlled_Buffer controlled_buffer_4
  assign updated_program = and_7_out ? cur_command : 8'bz;  // Controlled_Buffer controlled_buffer_5
  assign updated_program = and_8_out ? cur_command : 8'bz;  // Controlled_Buffer controlled_buffer_6
  assign updated_program = repeated_command ? cur_command : 8'bz;  // Controlled_Buffer controlled_buffer_7

  // Other names for the same wires on the sheet: case2[3:0] = cur_command[3:0]; case3[7:0] = cur_command;
  //   command[7:0] = cur_command; case1[7:4] = cur_command[7:4]; not_equal = repeated_command;
  //   res[7:0] = updated_program
endmodule

module _4_colod (
  input  _4,
  input  [7:0] cur_command,
  output [7:0] updated_program,
  output repeated_command,
  output move_done_updated
);

  wire _1st_done, _2st_done, and_1_out, and_2_out, and_3_out, and_4_out, and_5_out, and_6_out, and_7_out,
       and_8_out, or_3_out, or_4_out;

  Comparator #(.width(4), .mode("unsigned")) comparator_1 (
    .a(4'b0100), .b(cur_command[3:0]), .eq(repeated_command));  // open: gt, lt
  or or_1 (_1st_done, cur_command[0], cur_command[1], cur_command[2], cur_command[3]);
  or or_2 (_2st_done, cur_command[4], cur_command[5], cur_command[6], cur_command[7]);
  and and_1 (and_1_out, _1st_done, _2st_done);
  or or_3 (or_3_out, updated_program[0], updated_program[1], updated_program[2], updated_program[3]);
  and and_2 (and_2_out, or_3_out, or_4_out);
  or or_4 (or_4_out, updated_program[4], updated_program[5], updated_program[6], updated_program[7]);
  or or_5 (move_done_updated, and_1_out, and_2_out);
  and and_3 (and_3_out, _1st_done, _4, _2st_done, ~repeated_command);  // AND_Gate
  and and_4 (and_4_out, _1st_done, ~_4, _2st_done, ~repeated_command);  // AND_Gate
  and and_5 (and_5_out, _1st_done, _4, ~_2st_done, ~repeated_command);  // AND_Gate
  and and_6 (and_6_out, ~_1st_done, _4, ~_2st_done, ~repeated_command);  // AND_Gate
  and and_7 (and_7_out, _1st_done, ~_4, ~_2st_done, ~repeated_command);  // AND_Gate
  and and_8 (and_8_out, ~_1st_done, ~_4, ~_2st_done, ~repeated_command);  // AND_Gate
  assign updated_program = and_3_out ? cur_command : 8'bz;  // Controlled_Buffer controlled_buffer_1
  assign updated_program = and_4_out ? cur_command : 8'bz;  // Controlled_Buffer controlled_buffer_2
  assign updated_program = and_5_out ? {4'b0100, cur_command[3:0]} : 8'bz;  // Controlled_Buffer controlled_buffer_3
  assign updated_program = and_6_out ? {cur_command[7:4], 4'b0100} : 8'bz;  // Controlled_Buffer controlled_buffer_4
  assign updated_program = and_7_out ? cur_command : 8'bz;  // Controlled_Buffer controlled_buffer_5
  assign updated_program = and_8_out ? cur_command : 8'bz;  // Controlled_Buffer controlled_buffer_6
  assign updated_program = repeated_command ? cur_command : 8'bz;  // Controlled_Buffer controlled_buffer_7

  // Other names for the same wires on the sheet: case2[3:0] = cur_command[3:0]; case3[7:0] = cur_command;
  //   command[7:0] = cur_command; case1[7:4] = cur_command[7:4]; not_equal = repeated_command;
  //   res[7:0] = updated_program
endmodule

module _5_colod (
  input  _5,
  input  [7:0] cur_command,
  output [7:0] updated_program,
  output repeated_command,
  output move_done_updated
);

  wire _1st_done, _2st_done, and_1_out, and_2_out, and_3_out, and_4_out, and_5_out, and_6_out, and_7_out,
       and_8_out, or_3_out, or_4_out;

  Comparator #(.width(4), .mode("unsigned")) comparator_1 (
    .a(4'b0101), .b(cur_command[3:0]), .eq(repeated_command));  // open: gt, lt
  or or_1 (_1st_done, cur_command[0], cur_command[1], cur_command[2], cur_command[3]);
  or or_2 (_2st_done, cur_command[4], cur_command[5], cur_command[6], cur_command[7]);
  and and_1 (and_1_out, _1st_done, _2st_done);
  or or_3 (or_3_out, updated_program[0], updated_program[1], updated_program[2], updated_program[3]);
  and and_2 (and_2_out, or_3_out, or_4_out);
  or or_4 (or_4_out, updated_program[4], updated_program[5], updated_program[6], updated_program[7]);
  or or_5 (move_done_updated, and_1_out, and_2_out);
  and and_3 (and_3_out, _1st_done, _5, _2st_done, ~repeated_command);  // AND_Gate
  and and_4 (and_4_out, _1st_done, ~_5, _2st_done, ~repeated_command);  // AND_Gate
  and and_5 (and_5_out, _1st_done, _5, ~_2st_done, ~repeated_command);  // AND_Gate
  and and_6 (and_6_out, ~_1st_done, _5, ~_2st_done, ~repeated_command);  // AND_Gate
  and and_7 (and_7_out, _1st_done, ~_5, ~_2st_done, ~repeated_command);  // AND_Gate
  and and_8 (and_8_out, ~_1st_done, ~_5, ~_2st_done, ~repeated_command);  // AND_Gate
  assign updated_program = and_3_out ? cur_command : 8'bz;  // Controlled_Buffer controlled_buffer_1
  assign updated_program = and_4_out ? cur_command : 8'bz;  // Controlled_Buffer controlled_buffer_2
  assign updated_program = and_5_out ? {4'b0101, cur_command[3:0]} : 8'bz;  // Controlled_Buffer controlled_buffer_3
  assign updated_program = and_6_out ? {cur_command[7:4], 4'b0101} : 8'bz;  // Controlled_Buffer controlled_buffer_4
  assign updated_program = and_7_out ? cur_command : 8'bz;  // Controlled_Buffer controlled_buffer_5
  assign updated_program = and_8_out ? cur_command : 8'bz;  // Controlled_Buffer controlled_buffer_6
  assign updated_program = repeated_command ? cur_command : 8'bz;  // Controlled_Buffer controlled_buffer_7

  // Other names for the same wires on the sheet: case2[3:0] = cur_command[3:0]; case3[7:0] = cur_command;
  //   command[7:0] = cur_command; case1[7:4] = cur_command[7:4]; not_equal = repeated_command;
  //   res[7:0] = updated_program
endmodule

module _6_colod (
  input  _6,
  input  [7:0] cur_command,
  output [7:0] updated_program,
  output repeated_command,
  output move_done_updated
);

  wire _1st_done, _2st_done, and_1_out, and_2_out, and_3_out, and_4_out, and_5_out, and_6_out, and_7_out,
       and_8_out, or_3_out, or_4_out;

  Comparator #(.width(4), .mode("unsigned")) comparator_1 (
    .a(4'b0110), .b(cur_command[3:0]), .eq(repeated_command));  // open: gt, lt
  or or_1 (_1st_done, cur_command[0], cur_command[1], cur_command[2], cur_command[3]);
  or or_2 (_2st_done, cur_command[4], cur_command[5], cur_command[6], cur_command[7]);
  and and_1 (and_1_out, _1st_done, _2st_done);
  or or_3 (or_3_out, updated_program[0], updated_program[1], updated_program[2], updated_program[3]);
  and and_2 (and_2_out, or_3_out, or_4_out);
  or or_4 (or_4_out, updated_program[4], updated_program[5], updated_program[6], updated_program[7]);
  or or_5 (move_done_updated, and_1_out, and_2_out);
  and and_3 (and_3_out, _1st_done, _6, _2st_done, ~repeated_command);  // AND_Gate
  and and_4 (and_4_out, _1st_done, ~_6, _2st_done, ~repeated_command);  // AND_Gate
  and and_5 (and_5_out, _1st_done, _6, ~_2st_done, ~repeated_command);  // AND_Gate
  and and_6 (and_6_out, ~_1st_done, _6, ~_2st_done, ~repeated_command);  // AND_Gate
  and and_7 (and_7_out, _1st_done, ~_6, ~_2st_done, ~repeated_command);  // AND_Gate
  and and_8 (and_8_out, ~_1st_done, ~_6, ~_2st_done, ~repeated_command);  // AND_Gate
  assign updated_program = and_3_out ? cur_command : 8'bz;  // Controlled_Buffer controlled_buffer_1
  assign updated_program = and_4_out ? cur_command : 8'bz;  // Controlled_Buffer controlled_buffer_2
  assign updated_program = and_5_out ? {4'b0110, cur_command[3:0]} : 8'bz;  // Controlled_Buffer controlled_buffer_3
  assign updated_program = and_6_out ? {cur_command[7:4], 4'b0110} : 8'bz;  // Controlled_Buffer controlled_buffer_4
  assign updated_program = and_7_out ? cur_command : 8'bz;  // Controlled_Buffer controlled_buffer_5
  assign updated_program = and_8_out ? cur_command : 8'bz;  // Controlled_Buffer controlled_buffer_6
  assign updated_program = repeated_command ? cur_command : 8'bz;  // Controlled_Buffer controlled_buffer_7

  // Other names for the same wires on the sheet: case2[3:0] = cur_command[3:0]; case3[7:0] = cur_command;
  //   command[7:0] = cur_command; case1[7:4] = cur_command[7:4]; not_equal = repeated_command;
  //   res[7:0] = updated_program
endmodule

module _7_colod (
  input  _7,
  input  [7:0] cur_command,
  output [7:0] updated_program,
  output repeated_command,
  output move_done_updated
);

  wire _1st_done, _2st_done, and_1_out, and_2_out, and_3_out, and_4_out, and_5_out, and_6_out, and_7_out,
       and_8_out, or_3_out, or_4_out;

  Comparator #(.width(4), .mode("unsigned")) comparator_1 (
    .a(4'b0111), .b(cur_command[3:0]), .eq(repeated_command));  // open: gt, lt
  or or_1 (_1st_done, cur_command[0], cur_command[1], cur_command[2], cur_command[3]);
  or or_2 (_2st_done, cur_command[4], cur_command[5], cur_command[6], cur_command[7]);
  and and_1 (and_1_out, _1st_done, _2st_done);
  or or_3 (or_3_out, updated_program[0], updated_program[1], updated_program[2], updated_program[3]);
  and and_2 (and_2_out, or_3_out, or_4_out);
  or or_4 (or_4_out, updated_program[4], updated_program[5], updated_program[6], updated_program[7]);
  or or_5 (move_done_updated, and_1_out, and_2_out);
  and and_3 (and_3_out, _1st_done, _7, _2st_done, ~repeated_command);  // AND_Gate
  and and_4 (and_4_out, _1st_done, ~_7, _2st_done, ~repeated_command);  // AND_Gate
  and and_5 (and_5_out, _1st_done, _7, ~_2st_done, ~repeated_command);  // AND_Gate
  and and_6 (and_6_out, ~_1st_done, _7, ~_2st_done, ~repeated_command);  // AND_Gate
  and and_7 (and_7_out, _1st_done, ~_7, ~_2st_done, ~repeated_command);  // AND_Gate
  and and_8 (and_8_out, ~_1st_done, ~_7, ~_2st_done, ~repeated_command);  // AND_Gate
  assign updated_program = and_3_out ? cur_command : 8'bz;  // Controlled_Buffer controlled_buffer_1
  assign updated_program = and_4_out ? cur_command : 8'bz;  // Controlled_Buffer controlled_buffer_2
  assign updated_program = and_5_out ? {4'b0111, cur_command[3:0]} : 8'bz;  // Controlled_Buffer controlled_buffer_3
  assign updated_program = and_6_out ? {cur_command[7:4], 4'b0111} : 8'bz;  // Controlled_Buffer controlled_buffer_4
  assign updated_program = and_7_out ? cur_command : 8'bz;  // Controlled_Buffer controlled_buffer_5
  assign updated_program = and_8_out ? cur_command : 8'bz;  // Controlled_Buffer controlled_buffer_6
  assign updated_program = repeated_command ? cur_command : 8'bz;  // Controlled_Buffer controlled_buffer_7

  // Other names for the same wires on the sheet: case2[3:0] = cur_command[3:0]; case3[7:0] = cur_command;
  //   command[7:0] = cur_command; case1[7:4] = cur_command[7:4]; not_equal = repeated_command;
  //   res[7:0] = updated_program
endmodule

module configuration (
  input  [31:0] colods,
  input  clock,
  output [31:0] final_colod,
  output [3:0] card
);

  wire _1, _2, _3, _4, _5, _6, _7, _8, _9, _10, _11, _12, _13, _14, _15, _16, _17, _18, _19, _20, _21, _22,
       _23, _24, _25, _26, _27, _28, _29, _30, _31, _32, bitfinder_1_found, bitfinder_2_found,
       bitfinder_3_found, bitfinder_4_found, bitfinder_5_found, bitfinder_6_found, bitfinder_7_found,
       bitfinder_8_found, bitfinder_9_found, bitfinder_10_found, bitfinder_11_found, bitfinder_12_found,
       bitfinder_13_found, bitfinder_14_found, bitfinder_15_found, bitfinder_16_found, bitfinder_17_found,
       bitfinder_18_found, bitfinder_19_found, bitfinder_20_found, bitfinder_21_found, bitfinder_22_found,
       bitfinder_23_found, bitfinder_24_found, bitfinder_25_found, bitfinder_26_found, bitfinder_27_found,
       bitfinder_28_found, bitfinder_29_found, bitfinder_30_found, bitfinder_31_found, bitfinder_32_found;
  wire [3:0] pull_resistor_33_node, pull_resistor_34_node, pull_resistor_35_node, pull_resistor_36_node,
       pull_resistor_37_node, pull_resistor_38_node, pull_resistor_39_node, pull_resistor_40_node,
       pull_resistor_41_node, pull_resistor_42_node, pull_resistor_43_node, pull_resistor_44_node,
       pull_resistor_45_node, pull_resistor_46_node, pull_resistor_47_node, pull_resistor_48_node,
       pull_resistor_49_node, pull_resistor_50_node, pull_resistor_51_node, pull_resistor_52_node,
       pull_resistor_53_node, pull_resistor_54_node, pull_resistor_55_node, pull_resistor_56_node,
       pull_resistor_57_node, pull_resistor_58_node, pull_resistor_59_node, pull_resistor_60_node,
       pull_resistor_61_node, pull_resistor_62_node, pull_resistor_63_node, pull_resistor_64_node;
  wire [4:0] random_1_out;
  wire [31:0] n1, n2, n3, n4, n5, n6, n7, n8, n9, n10, n11, n12, n13, n14, n15, n16, n17, n18, n19, n20, n21,
       n22, n23, n24, n25, n26, n27, n28, n29, n30, n31, n32, nor_1_out, pull_resistor_1_node,
       pull_resistor_2_node, pull_resistor_3_node, pull_resistor_4_node, pull_resistor_5_node,
       pull_resistor_6_node, pull_resistor_7_node, pull_resistor_8_node, pull_resistor_9_node,
       pull_resistor_10_node, pull_resistor_11_node, pull_resistor_12_node, pull_resistor_13_node,
       pull_resistor_14_node, pull_resistor_15_node, pull_resistor_16_node, pull_resistor_17_node,
       pull_resistor_18_node, pull_resistor_19_node, pull_resistor_20_node, pull_resistor_21_node,
       pull_resistor_22_node, pull_resistor_23_node, pull_resistor_24_node, pull_resistor_25_node,
       pull_resistor_26_node, pull_resistor_27_node, pull_resistor_28_node, pull_resistor_29_node,
       pull_resistor_30_node, pull_resistor_31_node, pull_resistor_32_node;

  Decoder #(.select(5), .enable("false")) decoder_1 (
    .out0(_1), .out1(_2), .out2(_3), .out3(_4), .out4(_5), .out5(_6), .out6(_7), .out7(_8), .out8(_9),
    .out9(_10), .out10(_11), .out11(_12), .out12(_13), .out13(_14), .out14(_15), .out15(_16), .out16(_17),
    .out17(_18), .out18(_19), .out19(_20), .out20(_21), .out21(_22), .out22(_23), .out23(_24), .out24(_25),
    .out25(_26), .out26(_27), .out27(_28), .out28(_29), .out29(_30), .out30(_31), .out31(_32),
    .sel(random_1_out));
  Random #(.width(5)) random_1 (.clk(clock), .out(random_1_out));  // open: next, clr
  assign nor_1_out = ~(n1 | n2 | n3 | n4 | n5 | n6 | n7 | n8 | n9 | n10 | n11 | n12 | n13 | n14 | n15 | n16 | n17 | n18 | n19 | n20 | n21 | n22 | n23 | n24 | n25 | n26 | n27 | n28 | n29 | n30 | n31 | n32);  // NOR_Gate nor_1, 32 bits wide
  assign final_colod = nor_1_out & colods;  // AND_Gate and_1, 32 bits wide
  Pull_Resistor pull_resistor_1 (.node(pull_resistor_1_node));
  Pull_Resistor pull_resistor_2 (.node(pull_resistor_2_node));
  Pull_Resistor pull_resistor_3 (.node(pull_resistor_3_node));
  Pull_Resistor pull_resistor_4 (.node(pull_resistor_4_node));
  Pull_Resistor pull_resistor_5 (.node(pull_resistor_5_node));
  Pull_Resistor pull_resistor_6 (.node(pull_resistor_6_node));
  Pull_Resistor pull_resistor_7 (.node(pull_resistor_7_node));
  Pull_Resistor pull_resistor_8 (.node(pull_resistor_8_node));
  Pull_Resistor pull_resistor_9 (.node(pull_resistor_9_node));
  Pull_Resistor pull_resistor_10 (.node(pull_resistor_10_node));
  Pull_Resistor pull_resistor_11 (.node(pull_resistor_11_node));
  Pull_Resistor pull_resistor_12 (.node(pull_resistor_12_node));
  Pull_Resistor pull_resistor_13 (.node(pull_resistor_13_node));
  Pull_Resistor pull_resistor_14 (.node(pull_resistor_14_node));
  Pull_Resistor pull_resistor_15 (.node(pull_resistor_15_node));
  Pull_Resistor pull_resistor_16 (.node(pull_resistor_16_node));
  Pull_Resistor pull_resistor_17 (.node(pull_resistor_17_node));
  Pull_Resistor pull_resistor_18 (.node(pull_resistor_18_node));
  Pull_Resistor pull_resistor_19 (.node(pull_resistor_19_node));
  Pull_Resistor pull_resistor_20 (.node(pull_resistor_20_node));
  Pull_Resistor pull_resistor_21 (.node(pull_resistor_21_node));
  Pull_Resistor pull_resistor_22 (.node(pull_resistor_22_node));
  Pull_Resistor pull_resistor_23 (.node(pull_resistor_23_node));
  Pull_Resistor pull_resistor_24 (.node(pull_resistor_24_node));
  Pull_Resistor pull_resistor_25 (.node(pull_resistor_25_node));
  Pull_Resistor pull_resistor_26 (.node(pull_resistor_26_node));
  Pull_Resistor pull_resistor_27 (.node(pull_resistor_27_node));
  Pull_Resistor pull_resistor_28 (.node(pull_resistor_28_node));
  Pull_Resistor pull_resistor_29 (.node(pull_resistor_29_node));
  Pull_Resistor pull_resistor_30 (.node(pull_resistor_30_node));
  Pull_Resistor pull_resistor_31 (.node(pull_resistor_31_node));
  Pull_Resistor pull_resistor_32 (.node(pull_resistor_32_node));
  assign pull_resistor_1_node = _1 ? 32'h1 : 32'bz;  // Controlled_Buffer controlled_buffer_1
  assign pull_resistor_2_node = _2 ? 32'h2 : 32'bz;  // Controlled_Buffer controlled_buffer_2
  assign pull_resistor_3_node = _3 ? 32'h4 : 32'bz;  // Controlled_Buffer controlled_buffer_3
  assign pull_resistor_4_node = _4 ? 32'h8 : 32'bz;  // Controlled_Buffer controlled_buffer_4
  assign pull_resistor_5_node = _5 ? 32'h10 : 32'bz;  // Controlled_Buffer controlled_buffer_5
  assign pull_resistor_6_node = _6 ? 32'h20 : 32'bz;  // Controlled_Buffer controlled_buffer_6
  assign pull_resistor_7_node = _7 ? 32'h40 : 32'bz;  // Controlled_Buffer controlled_buffer_7
  assign pull_resistor_8_node = _8 ? 32'h80 : 32'bz;  // Controlled_Buffer controlled_buffer_8
  assign pull_resistor_9_node = _9 ? 32'h100 : 32'bz;  // Controlled_Buffer controlled_buffer_9
  assign pull_resistor_10_node = _10 ? 32'h200 : 32'bz;  // Controlled_Buffer controlled_buffer_10
  assign pull_resistor_11_node = _11 ? 32'h400 : 32'bz;  // Controlled_Buffer controlled_buffer_11
  assign pull_resistor_12_node = _12 ? 32'h800 : 32'bz;  // Controlled_Buffer controlled_buffer_12
  assign pull_resistor_13_node = _13 ? 32'h1000 : 32'bz;  // Controlled_Buffer controlled_buffer_13
  assign pull_resistor_14_node = _14 ? 32'h2000 : 32'bz;  // Controlled_Buffer controlled_buffer_14
  assign pull_resistor_15_node = _15 ? 32'h4000 : 32'bz;  // Controlled_Buffer controlled_buffer_15
  assign pull_resistor_16_node = _16 ? 32'h8000 : 32'bz;  // Controlled_Buffer controlled_buffer_16
  assign pull_resistor_17_node = _17 ? 32'h10000 : 32'bz;  // Controlled_Buffer controlled_buffer_17
  assign pull_resistor_18_node = _18 ? 32'h20000 : 32'bz;  // Controlled_Buffer controlled_buffer_18
  assign pull_resistor_19_node = _19 ? 32'h40000 : 32'bz;  // Controlled_Buffer controlled_buffer_19
  assign pull_resistor_20_node = _20 ? 32'h80000 : 32'bz;  // Controlled_Buffer controlled_buffer_20
  assign pull_resistor_21_node = _21 ? 32'h100000 : 32'bz;  // Controlled_Buffer controlled_buffer_21
  assign pull_resistor_22_node = _22 ? 32'h200000 : 32'bz;  // Controlled_Buffer controlled_buffer_22
  assign pull_resistor_23_node = _23 ? 32'h400000 : 32'bz;  // Controlled_Buffer controlled_buffer_23
  assign pull_resistor_24_node = _24 ? 32'h800000 : 32'bz;  // Controlled_Buffer controlled_buffer_24
  assign pull_resistor_25_node = _25 ? 32'h1000000 : 32'bz;  // Controlled_Buffer controlled_buffer_25
  assign pull_resistor_26_node = _26 ? 32'h2000000 : 32'bz;  // Controlled_Buffer controlled_buffer_26
  assign pull_resistor_27_node = _27 ? 32'h4000000 : 32'bz;  // Controlled_Buffer controlled_buffer_27
  assign pull_resistor_28_node = _28 ? 32'h8000000 : 32'bz;  // Controlled_Buffer controlled_buffer_28
  assign pull_resistor_29_node = _29 ? 32'h10000000 : 32'bz;  // Controlled_Buffer controlled_buffer_29
  assign pull_resistor_30_node = _30 ? 32'h20000000 : 32'bz;  // Controlled_Buffer controlled_buffer_30
  assign pull_resistor_31_node = _31 ? 32'h40000000 : 32'bz;  // Controlled_Buffer controlled_buffer_31
  assign pull_resistor_32_node = _32 ? 32'h80000000 : 32'bz;  // Controlled_Buffer controlled_buffer_32
  assign n1 = pull_resistor_1_node & colods;  // AND_Gate and_2, 32 bits wide
  assign n2 = pull_resistor_2_node & colods;  // AND_Gate and_3, 32 bits wide
  assign n3 = pull_resistor_3_node & colods;  // AND_Gate and_4, 32 bits wide
  assign n4 = pull_resistor_4_node & colods;  // AND_Gate and_5, 32 bits wide
  assign n5 = pull_resistor_5_node & colods;  // AND_Gate and_6, 32 bits wide
  assign n6 = pull_resistor_6_node & colods;  // AND_Gate and_7, 32 bits wide
  assign n7 = pull_resistor_7_node & colods;  // AND_Gate and_8, 32 bits wide
  assign n8 = pull_resistor_8_node & colods;  // AND_Gate and_9, 32 bits wide
  assign n9 = pull_resistor_9_node & colods;  // AND_Gate and_10, 32 bits wide
  assign n10 = pull_resistor_10_node & colods;  // AND_Gate and_11, 32 bits wide
  assign n11 = pull_resistor_11_node & colods;  // AND_Gate and_12, 32 bits wide
  assign n12 = pull_resistor_12_node & colods;  // AND_Gate and_13, 32 bits wide
  assign n13 = pull_resistor_13_node & colods;  // AND_Gate and_14, 32 bits wide
  assign n14 = pull_resistor_14_node & colods;  // AND_Gate and_15, 32 bits wide
  assign n15 = pull_resistor_15_node & colods;  // AND_Gate and_16, 32 bits wide
  assign n16 = pull_resistor_16_node & colods;  // AND_Gate and_17, 32 bits wide
  assign n17 = pull_resistor_17_node & colods;  // AND_Gate and_18, 32 bits wide
  assign n18 = pull_resistor_18_node & colods;  // AND_Gate and_19, 32 bits wide
  assign n19 = pull_resistor_19_node & colods;  // AND_Gate and_20, 32 bits wide
  assign n20 = pull_resistor_20_node & colods;  // AND_Gate and_21, 32 bits wide
  assign n21 = pull_resistor_21_node & colods;  // AND_Gate and_22, 32 bits wide
  assign n22 = pull_resistor_22_node & colods;  // AND_Gate and_23, 32 bits wide
  assign n23 = pull_resistor_23_node & colods;  // AND_Gate and_24, 32 bits wide
  assign n24 = pull_resistor_24_node & colods;  // AND_Gate and_25, 32 bits wide
  assign n25 = pull_resistor_25_node & colods;  // AND_Gate and_26, 32 bits wide
  assign n26 = pull_resistor_26_node & colods;  // AND_Gate and_27, 32 bits wide
  assign n27 = pull_resistor_27_node & colods;  // AND_Gate and_28, 32 bits wide
  assign n28 = pull_resistor_28_node & colods;  // AND_Gate and_29, 32 bits wide
  assign n29 = pull_resistor_29_node & colods;  // AND_Gate and_30, 32 bits wide
  assign n30 = pull_resistor_30_node & colods;  // AND_Gate and_31, 32 bits wide
  assign n31 = pull_resistor_31_node & colods;  // AND_Gate and_32, 32 bits wide
  assign n32 = pull_resistor_32_node & colods;  // AND_Gate and_33, 32 bits wide
  BitFinder #(.width(32)) bitfinder_1 (.in(n1), .found(bitfinder_1_found));  // open: index
  BitFinder #(.width(32)) bitfinder_2 (.in(n2), .found(bitfinder_2_found));  // open: index
  BitFinder #(.width(32)) bitfinder_3 (.in(n3), .found(bitfinder_3_found));  // open: index
  BitFinder #(.width(32)) bitfinder_4 (.in(n4), .found(bitfinder_4_found));  // open: index
  BitFinder #(.width(32)) bitfinder_5 (.in(n5), .found(bitfinder_5_found));  // open: index
  BitFinder #(.width(32)) bitfinder_6 (.in(n6), .found(bitfinder_6_found));  // open: index
  BitFinder #(.width(32)) bitfinder_7 (.in(n7), .found(bitfinder_7_found));  // open: index
  BitFinder #(.width(32)) bitfinder_8 (.in(n8), .found(bitfinder_8_found));  // open: index
  BitFinder #(.width(32)) bitfinder_9 (.in(n9), .found(bitfinder_9_found));  // open: index
  BitFinder #(.width(32)) bitfinder_10 (.in(n10), .found(bitfinder_10_found));  // open: index
  BitFinder #(.width(32)) bitfinder_11 (.in(n11), .found(bitfinder_11_found));  // open: index
  BitFinder #(.width(32)) bitfinder_12 (.in(n12), .found(bitfinder_12_found));  // open: index
  BitFinder #(.width(32)) bitfinder_13 (.in(n13), .found(bitfinder_13_found));  // open: index
  BitFinder #(.width(32)) bitfinder_14 (.in(n14), .found(bitfinder_14_found));  // open: index
  BitFinder #(.width(32)) bitfinder_15 (.in(n15), .found(bitfinder_15_found));  // open: index
  BitFinder #(.width(32)) bitfinder_16 (.in(n16), .found(bitfinder_16_found));  // open: index
  BitFinder #(.width(32)) bitfinder_17 (.in(n17), .found(bitfinder_17_found));  // open: index
  BitFinder #(.width(32)) bitfinder_18 (.in(n18), .found(bitfinder_18_found));  // open: index
  BitFinder #(.width(32)) bitfinder_19 (.in(n19), .found(bitfinder_19_found));  // open: index
  BitFinder #(.width(32)) bitfinder_20 (.in(n20), .found(bitfinder_20_found));  // open: index
  BitFinder #(.width(32)) bitfinder_21 (.in(n21), .found(bitfinder_21_found));  // open: index
  BitFinder #(.width(32)) bitfinder_22 (.in(n22), .found(bitfinder_22_found));  // open: index
  BitFinder #(.width(32)) bitfinder_23 (.in(n23), .found(bitfinder_23_found));  // open: index
  BitFinder #(.width(32)) bitfinder_24 (.in(n24), .found(bitfinder_24_found));  // open: index
  BitFinder #(.width(32)) bitfinder_25 (.in(n25), .found(bitfinder_25_found));  // open: index
  BitFinder #(.width(32)) bitfinder_26 (.in(n26), .found(bitfinder_26_found));  // open: index
  BitFinder #(.width(32)) bitfinder_27 (.in(n27), .found(bitfinder_27_found));  // open: index
  BitFinder #(.width(32)) bitfinder_28 (.in(n28), .found(bitfinder_28_found));  // open: index
  BitFinder #(.width(32)) bitfinder_29 (.in(n29), .found(bitfinder_29_found));  // open: index
  BitFinder #(.width(32)) bitfinder_30 (.in(n30), .found(bitfinder_30_found));  // open: index
  BitFinder #(.width(32)) bitfinder_31 (.in(n31), .found(bitfinder_31_found));  // open: index
  BitFinder #(.width(32)) bitfinder_32 (.in(n32), .found(bitfinder_32_found));  // open: index
  Pull_Resistor pull_resistor_33 (.node(pull_resistor_33_node));
  assign pull_resistor_33_node = bitfinder_1_found ? 4'b0010 : 4'bz;  // Controlled_Buffer controlled_buffer_33
  Pull_Resistor pull_resistor_34 (.node(pull_resistor_34_node));
  assign pull_resistor_34_node = bitfinder_2_found ? 4'b0011 : 4'bz;  // Controlled_Buffer controlled_buffer_34
  Pull_Resistor pull_resistor_35 (.node(pull_resistor_35_node));
  assign pull_resistor_35_node = bitfinder_3_found ? 4'b0100 : 4'bz;  // Controlled_Buffer controlled_buffer_35
  Pull_Resistor pull_resistor_36 (.node(pull_resistor_36_node));
  assign pull_resistor_36_node = bitfinder_4_found ? 4'b0101 : 4'bz;  // Controlled_Buffer controlled_buffer_36
  Pull_Resistor pull_resistor_37 (.node(pull_resistor_37_node));
  assign pull_resistor_37_node = bitfinder_5_found ? 4'b0110 : 4'bz;  // Controlled_Buffer controlled_buffer_37
  Pull_Resistor pull_resistor_38 (.node(pull_resistor_38_node));
  assign pull_resistor_38_node = bitfinder_6_found ? 4'b0111 : 4'bz;  // Controlled_Buffer controlled_buffer_38
  Pull_Resistor pull_resistor_39 (.node(pull_resistor_39_node));
  assign pull_resistor_39_node = bitfinder_7_found ? 4'b1000 : 4'bz;  // Controlled_Buffer controlled_buffer_39
  Pull_Resistor pull_resistor_40 (.node(pull_resistor_40_node));
  assign pull_resistor_40_node = bitfinder_8_found ? 4'b1001 : 4'bz;  // Controlled_Buffer controlled_buffer_40
  Pull_Resistor pull_resistor_41 (.node(pull_resistor_41_node));
  assign pull_resistor_41_node = bitfinder_9_found ? 4'b0010 : 4'bz;  // Controlled_Buffer controlled_buffer_41
  Pull_Resistor pull_resistor_42 (.node(pull_resistor_42_node));
  assign pull_resistor_42_node = bitfinder_10_found ? 4'b0011 : 4'bz;  // Controlled_Buffer controlled_buffer_42
  Pull_Resistor pull_resistor_43 (.node(pull_resistor_43_node));
  assign pull_resistor_43_node = bitfinder_11_found ? 4'b0100 : 4'bz;  // Controlled_Buffer controlled_buffer_43
  Pull_Resistor pull_resistor_44 (.node(pull_resistor_44_node));
  assign pull_resistor_44_node = bitfinder_12_found ? 4'b0101 : 4'bz;  // Controlled_Buffer controlled_buffer_44
  Pull_Resistor pull_resistor_45 (.node(pull_resistor_45_node));
  assign pull_resistor_45_node = bitfinder_13_found ? 4'b0110 : 4'bz;  // Controlled_Buffer controlled_buffer_45
  Pull_Resistor pull_resistor_46 (.node(pull_resistor_46_node));
  assign pull_resistor_46_node = bitfinder_14_found ? 4'b0111 : 4'bz;  // Controlled_Buffer controlled_buffer_46
  Pull_Resistor pull_resistor_47 (.node(pull_resistor_47_node));
  assign pull_resistor_47_node = bitfinder_15_found ? 4'b1000 : 4'bz;  // Controlled_Buffer controlled_buffer_47
  Pull_Resistor pull_resistor_48 (.node(pull_resistor_48_node));
  assign pull_resistor_48_node = bitfinder_16_found ? 4'b1001 : 4'bz;  // Controlled_Buffer controlled_buffer_48
  Pull_Resistor pull_resistor_49 (.node(pull_resistor_49_node));
  assign pull_resistor_49_node = bitfinder_17_found ? 4'b0010 : 4'bz;  // Controlled_Buffer controlled_buffer_49
  Pull_Resistor pull_resistor_50 (.node(pull_resistor_50_node));
  assign pull_resistor_50_node = bitfinder_18_found ? 4'b0011 : 4'bz;  // Controlled_Buffer controlled_buffer_50
  Pull_Resistor pull_resistor_51 (.node(pull_resistor_51_node));
  assign pull_resistor_51_node = bitfinder_19_found ? 4'b0100 : 4'bz;  // Controlled_Buffer controlled_buffer_51
  Pull_Resistor pull_resistor_52 (.node(pull_resistor_52_node));
  assign pull_resistor_52_node = bitfinder_20_found ? 4'b0101 : 4'bz;  // Controlled_Buffer controlled_buffer_52
  Pull_Resistor pull_resistor_53 (.node(pull_resistor_53_node));
  assign pull_resistor_53_node = bitfinder_21_found ? 4'b0110 : 4'bz;  // Controlled_Buffer controlled_buffer_53
  Pull_Resistor pull_resistor_54 (.node(pull_resistor_54_node));
  assign pull_resistor_54_node = bitfinder_22_found ? 4'b0111 : 4'bz;  // Controlled_Buffer controlled_buffer_54
  Pull_Resistor pull_resistor_55 (.node(pull_resistor_55_node));
  assign pull_resistor_55_node = bitfinder_23_found ? 4'b1000 : 4'bz;  // Controlled_Buffer controlled_buffer_55
  Pull_Resistor pull_resistor_56 (.node(pull_resistor_56_node));
  assign pull_resistor_56_node = bitfinder_24_found ? 4'b1001 : 4'bz;  // Controlled_Buffer controlled_buffer_56
  Pull_Resistor pull_resistor_57 (.node(pull_resistor_57_node));
  assign pull_resistor_57_node = bitfinder_25_found ? 4'b0010 : 4'bz;  // Controlled_Buffer controlled_buffer_57
  Pull_Resistor pull_resistor_58 (.node(pull_resistor_58_node));
  assign pull_resistor_58_node = bitfinder_26_found ? 4'b0011 : 4'bz;  // Controlled_Buffer controlled_buffer_58
  Pull_Resistor pull_resistor_59 (.node(pull_resistor_59_node));
  assign pull_resistor_59_node = bitfinder_27_found ? 4'b0100 : 4'bz;  // Controlled_Buffer controlled_buffer_59
  Pull_Resistor pull_resistor_60 (.node(pull_resistor_60_node));
  assign pull_resistor_60_node = bitfinder_28_found ? 4'b0101 : 4'bz;  // Controlled_Buffer controlled_buffer_60
  Pull_Resistor pull_resistor_61 (.node(pull_resistor_61_node));
  assign pull_resistor_61_node = bitfinder_29_found ? 4'b0110 : 4'bz;  // Controlled_Buffer controlled_buffer_61
  Pull_Resistor pull_resistor_62 (.node(pull_resistor_62_node));
  assign pull_resistor_62_node = bitfinder_30_found ? 4'b0111 : 4'bz;  // Controlled_Buffer controlled_buffer_62
  Pull_Resistor pull_resistor_63 (.node(pull_resistor_63_node));
  assign pull_resistor_63_node = bitfinder_31_found ? 4'b1000 : 4'bz;  // Controlled_Buffer controlled_buffer_63
  Pull_Resistor pull_resistor_64 (.node(pull_resistor_64_node));
  assign pull_resistor_64_node = bitfinder_32_found ? 4'b1001 : 4'bz;  // Controlled_Buffer controlled_buffer_64
  assign card = pull_resistor_33_node | pull_resistor_34_node | pull_resistor_35_node | pull_resistor_36_node | pull_resistor_37_node | pull_resistor_38_node | pull_resistor_39_node | pull_resistor_40_node | pull_resistor_41_node | pull_resistor_42_node | pull_resistor_43_node | pull_resistor_44_node | pull_resistor_45_node | pull_resistor_46_node | pull_resistor_47_node | pull_resistor_48_node | pull_resistor_49_node | pull_resistor_50_node | pull_resistor_51_node | pull_resistor_52_node | pull_resistor_53_node | pull_resistor_54_node | pull_resistor_55_node | pull_resistor_56_node | pull_resistor_57_node | pull_resistor_58_node | pull_resistor_59_node | pull_resistor_60_node | pull_resistor_61_node | pull_resistor_62_node | pull_resistor_63_node | pull_resistor_64_node;  // OR_Gate or_1, 4 bits wide
endmodule

module generator (
  input  clock,
  input  reset,
  output [7:0] address,
  output [7:0] data,
  output l_d,
  output clock_gen,
  output gen_done
);

  wire bitfinder_1_found, comparator_1_eq, comparator_2_eq, comparator_3_eq, comparator_4_eq,
       comparator_5_eq, comparator_6_eq, comparator_7_eq, comparator_8_gt, comparator_9_eq, comparator_10_eq,
       comparator_12_eq, eq_0, not_1_out, not_2_out, not_3_out, not_4_out, not_5_out, or_1_out, or_2_out,
       tact;
  wire [3:0] configuration_1_card;
  wire [4:0] adder_1_out, multiplexer_2_out, register_1_q;
  wire [7:0] addr, counter_1_q, counter_2_q;
  wire [7:7] pull_resistor_1_node;
  wire [31:0] configuration_1_final_colod, multiplexer_3_out, multiplexer_4_out, pull_resistor_2_node;

  Multiplexer #(.select(5), .width(8), .disabled(0), .enable("false")) multiplexer_1 (
    .in0(8'h91), .in1(8'h92), .in2(8'h9a), .in3(8'h9b), .in4(8'h9c), .in5(8'ha4), .in6(8'ha5), .in7(8'ha6),
    .in8(8'ha7), .in9(8'haf), .in10(8'hb0), .in11(8'hb1), .in12(8'hb2), .in13(8'hb3), .in14(8'hbb),
    .in15(8'hbc), .in16(8'hbd), .in17(8'hbe), .in18(8'hbf), .in19(8'hc8), .in20(8'hc9), .in21(8'hca),
    .in22(8'hcb), .in23(8'hcc), .in24(8'hcd), .in25(8'hd6), .in26(8'hd7), .in27(8'hd8), .in28(8'hd9),
    .in29(8'hda), .in30(8'hdb), .in31(8'hdc), .out(addr), .sel(register_1_q));
  Multiplexer #(.width(5), .enable("false")) multiplexer_2 (
    .in0({5{1'b0}}), .in1(adder_1_out), .out(multiplexer_2_out), .sel(comparator_8_gt));
  and and_1 (tact, clock, gen_done);
  Adder #(.width(5)) adder_1 (.a(register_1_q), .b(5'b00001), .out(adder_1_out));  // open: cin, cout
  not not_1 (not_1_out, eq_0);
  Counter counter_1 (.D({8{1'b0}}), .Q(counter_1_q), .clk(tact), .clr(reset));  // open: load, count, carry
  Comparator comparator_1 (.a(8'h92), .b(addr), .eq(comparator_1_eq));  // open: gt, lt
  Comparator comparator_2 (.a(8'h9c), .b(addr), .eq(comparator_2_eq));  // open: gt, lt
  Comparator comparator_3 (.a(8'ha7), .b(addr), .eq(comparator_3_eq));  // open: gt, lt
  Comparator comparator_4 (.a(8'hb3), .b(addr), .eq(comparator_4_eq));  // open: gt, lt
  Comparator comparator_5 (.a(8'hbf), .b(addr), .eq(comparator_5_eq));  // open: gt, lt
  Comparator comparator_6 (.a(8'hcd), .b(addr), .eq(comparator_6_eq));  // open: gt, lt
  Comparator comparator_7 (.a(8'hdc), .b(addr), .eq(comparator_7_eq));  // open: gt, lt
  Register #(.width(5)) register_1 (
    .D(multiplexer_2_out), .en(not_1_out), .Q(register_1_q), .clk(not_2_out), .clr(reset));
  not not_2 (not_2_out, tact);
  Comparator #(.mode("unsigned")) comparator_8 (.a(counter_1_q), .b({8{1'b0}}), .gt(comparator_8_gt));  // open: eq, lt
  or or_1 (or_1_out, gen_done, comparator_9_eq);
  or or_2 (or_2_out, comparator_1_eq, comparator_2_eq, comparator_3_eq, comparator_4_eq, comparator_5_eq, comparator_6_eq, comparator_7_eq);
  Multiplexer #(.width(32)) multiplexer_3 (
    .in0({32{1'b1}}), .in1(multiplexer_4_out), .out(multiplexer_3_out), .sel(not_3_out));  // open: en
  Counter counter_2 (.Q(counter_2_q), .clk(tact), .clr(reset));  // open: load, D, count, carry
  assign address = or_1_out ? addr : 8'bz;  // Controlled_Buffer controlled_buffer_1
  Comparator #(.mode("unsigned")) comparator_9 (.a(8'hdc), .b(addr), .eq(comparator_9_eq));  // open: gt, lt
  Pull_Resistor #(.pull(1)) pull_resistor_1 (.node(pull_resistor_1_node[7]));
  assign pull_resistor_1_node[7] = or_2_out ? 1'b0 : 1'bz;  // Controlled_Buffer controlled_buffer_2
  Pull_Resistor #(.pull(1)) pull_resistor_2 (.node(pull_resistor_2_node));
  assign pull_resistor_2_node = bitfinder_1_found ? multiplexer_3_out : 32'bz;  // Controlled_Buffer controlled_buffer_3
  not not_3 (not_3_out, comparator_10_eq);
  Comparator #(.mode("unsigned")) comparator_10 (
    .a({8{1'b0}}), .b(counter_2_q), .eq(comparator_10_eq));  // open: gt, lt
  BitFinder bitfinder_1 (.in(counter_2_q), .found(bitfinder_1_found));  // open: index
  configuration configuration_1 (
    .colods(pull_resistor_2_node), .clock(clock), .final_colod(configuration_1_final_colod),
    .card(configuration_1_card));
  Multiplexer #(.width(32), .enable("false")) multiplexer_4 (
    .in0(pull_resistor_2_node), .in1(configuration_1_final_colod), .out(multiplexer_4_out), .sel(not_4_out));
  not not_4 (not_4_out, clock);
  assign l_d = gen_done ? eq_0 : 1'bz;  // Controlled_Buffer controlled_buffer_4
  assign clock_gen = gen_done ? not_5_out : 1'bz;  // Controlled_Buffer controlled_buffer_5
  not not_5 (not_5_out, clock);
  Hex_Digit_Display hex_digit_display_1 (.value(configuration_1_card));  // open: dp
  assign data = gen_done ? {pull_resistor_1_node[7], 3'b100, configuration_1_card} : 8'bz;  // Controlled_Buffer controlled_buffer_6
  Comparator #(.width(4)) comparator_11 (.a(4'b0000), .b(configuration_1_card), .eq(eq_0));  // open: gt, lt
  Comparator #(.width(32)) comparator_12 (
    .a({32{1'b0}}), .b(multiplexer_4_out), .eq(comparator_12_eq));  // open: gt, lt
  not not_6 (gen_done, comparator_12_eq);

  // Notes on the sheet:
  //   1 colon
  //   2 colon
  //   3 colon
  //   4 colon
  //   5 colon
  //   6 colon
  //   7 colon
  //   opened
  //   sentinels
  //   Купил нисан - ебись с ним сам
endmodule

module write_sentinels (
  input  clock,
  input  reset,
  output [7:0] address,
  output [7:0] data,
  output l_d,
  output clock_gen,
  output sent_writing_done
);

  wire comparator_1_gt, gen_done, not_1_out, not_2_out, tact;
  wire [2:0] adder_1_out, multiplexer_2_out, register_1_q;
  wire [7:0] addr, counter_1_q;

  Multiplexer #(.select(3), .width(8), .disabled(0), .enable("false")) multiplexer_1 (
    .in0(8'h90), .in1(8'h99), .in2(8'ha3), .in3(8'hae), .in4(8'hba), .in5(8'hc7), .in6(8'hd5),
    .in7({8{1'b1}}), .out(addr), .sel(register_1_q));
  Multiplexer #(.width(3), .enable("false")) multiplexer_2 (
    .in0(3'b000), .in1(adder_1_out), .out(multiplexer_2_out), .sel(comparator_1_gt));
  Counter counter_1 (.D({8{1'b0}}), .Q(counter_1_q), .clk(tact), .clr(reset));  // open: load, count, carry
  Adder #(.width(3)) adder_1 (.a(register_1_q), .b(3'b001), .out(adder_1_out));  // open: cin, cout
  Register #(.width(3)) register_1 (
    .D(multiplexer_2_out), .en(gen_done), .Q(register_1_q), .clk(not_1_out), .clr(reset));
  not not_1 (not_1_out, tact);
  assign address = gen_done ? addr : 8'bz;  // Controlled_Buffer controlled_buffer_1
  assign l_d = gen_done ? 1'b0 : 1'bz;  // Controlled_Buffer controlled_buffer_2
  assign clock_gen = gen_done ? not_2_out : 1'bz;  // Controlled_Buffer controlled_buffer_3
  not not_2 (not_2_out, clock);
  Comparator #(.mode("unsigned")) comparator_1 (.a(counter_1_q), .b({8{1'b0}}), .gt(comparator_1_gt));  // open: eq, lt
  assign data = gen_done ? 8'ha : 8'bz;  // Controlled_Buffer controlled_buffer_4
  Comparator #(.mode("unsigned")) comparator_2 (.a({8{1'b1}}), .b(addr), .eq(sent_writing_done));  // open: gt, lt
  and and_1 (tact, clock, gen_done);
  not not_3 (gen_done, sent_writing_done);

  // Notes on the sheet:
  //   Купил нисан - ебись с ним сам
  //   opened
  //   sentinels
endmodule

module card_replace (
  input  [2:0] colod_number,
  input  [7:0] cur_command,
  output [7:0] updated_program,
  output repeated_command,
  output move_done_updated
);

  wire _1st_done, _2st_done, and_1_out, and_2_out, and_3_out, and_4_out, and_5_out, and_6_out, and_7_out,
       and_8_out, colod_isnt_0, comparator_1_eq, or_3_out, or_4_out;

  not not_1 (colod_isnt_0, comparator_1_eq);
  Comparator #(.width(3), .mode("unsigned")) comparator_1 (
    .a(colod_number), .b(3'b000), .eq(comparator_1_eq));  // open: gt, lt
  Comparator #(.width(3), .mode("unsigned")) comparator_2 (
    .a(colod_number), .b(cur_command[2:0]), .eq(repeated_command));  // open: gt, lt
  or or_1 (_1st_done, cur_command[0], cur_command[1], cur_command[2], cur_command[3]);
  or or_2 (_2st_done, cur_command[4], cur_command[5], cur_command[6], cur_command[7]);
  and and_1 (and_1_out, _1st_done, _2st_done);
  or or_3 (or_3_out, updated_program[0], updated_program[1], updated_program[2], updated_program[3]);
  and and_2 (and_2_out, or_3_out, or_4_out);
  or or_4 (or_4_out, updated_program[4], updated_program[5], updated_program[6], updated_program[7]);
  or or_5 (move_done_updated, and_1_out, and_2_out);
  and and_3 (and_3_out, _1st_done, colod_isnt_0, _2st_done, ~repeated_command);  // AND_Gate
  and and_4 (and_4_out, _1st_done, ~colod_isnt_0, _2st_done, ~repeated_command);  // AND_Gate
  and and_5 (and_5_out, _1st_done, colod_isnt_0, ~_2st_done, ~repeated_command);  // AND_Gate
  and and_6 (and_6_out, ~_1st_done, colod_isnt_0, ~_2st_done, ~repeated_command);  // AND_Gate
  and and_7 (and_7_out, _1st_done, ~colod_isnt_0, ~_2st_done, ~repeated_command);  // AND_Gate
  and and_8 (and_8_out, ~_1st_done, ~colod_isnt_0, ~_2st_done, ~repeated_command);  // AND_Gate
  assign updated_program = and_3_out ? cur_command : 8'bz;  // Controlled_Buffer controlled_buffer_1
  assign updated_program = and_4_out ? cur_command : 8'bz;  // Controlled_Buffer controlled_buffer_2
  assign updated_program = and_5_out ? {1'b0, colod_number, cur_command[3:0]} : 8'bz;  // Controlled_Buffer controlled_buffer_3
  assign updated_program = and_6_out ? {cur_command[7:4], 1'b0, colod_number} : 8'bz;  // Controlled_Buffer controlled_buffer_4
  assign updated_program = and_7_out ? cur_command : 8'bz;  // Controlled_Buffer controlled_buffer_5
  assign updated_program = and_8_out ? cur_command : 8'bz;  // Controlled_Buffer controlled_buffer_6
  assign updated_program = repeated_command ? cur_command : 8'bz;  // Controlled_Buffer controlled_buffer_7

  // Other names for the same wires on the sheet: c[2:0] = colod_number;
  //   case1 (some bits) = {cur_command[7:4], colod_number}; case2[6:0] = {colod_number, cur_command[3:0]};
  //   case3[7:0] = cur_command; command[7:0] = cur_command; not_equal = repeated_command; res[7:0] = updated_program
endmodule
